# Fritzing sketch 140303 Firefly PhoneHome v4 (saved by Fritzing 0.8.7b)
circuit board: 18.1908cm x 10.0276cm
breadboards: 1

parts:
  Part1 = Electric Imp April
  Part2 = Arduino Uno (Rev3)
  JACK1 = 2.1mm Barrel Jack with Terminal Block
  BMP1 = BMP085 Breakout
  D1 = Diode [package=diode-1n4148]
  R2 = Resistor [tolerance=±5% resistance=10k package="0603 [SMD]"]
  S1 = Pushbutton [package="[THT]"]
  R3 = Resistor [tolerance=±5% resistance=1k package=THT]
  VCC1 = Battery block 9V
  LED1 = RGB LED (com. anode, rbg) [package="5 mm [THT]"]
  LED2 = RGB LED (com. cathode, rgb) [package="5 mm [THT]"]
  LED3 = RGB LED (com. cathode, rgb) [package="5 mm [THT]"]

nets:
  N1: Part1.4, Part2.D1/TX
  N2: Part1.9, R2.Pin_1
  N3: Part1.10, Part2.D8, Part2.3V3, D1.C, S1.Pin_3, S1.Pin_4, R3.Pin_0
  N4: Part1.11, S1.Pin_1, S1.Pin_2
  N5: Part2.A4/SDA, BMP1.SDA
  N6: Part2.A5/SCL, BMP1.SCL
  N7: Part2.D12/MISO, LED1.green_cathode, LED2.blue_anode, LED3.blue_anode
  GND: Part2.GND, BMP1.GND, LED1.common_anode, LED2.common_cathode, LED3.common_cathode
  N8: JACK1.POS, VCC1.+
  N9: JACK1.NEG, VCC1.-
  N10: BMP1.VIN, R3.Pin_1

custom parts:
  Electric Imp April: Electric Imp Breakout Board with onboard 3.3V regulated power supply
  BMP085 Breakout: A breakout for the BMP085 barometric pressure and temperature sensor
